// Digital circuit Equals.dig as structural Verilog
module Equals (
  input  a,
  input  b,
  output y
);

  wire and_1_out, and_2_out, or_1_out;

  and and_1 (and_1_out, a, ~b);  // And
  and and_2 (and_2_out, ~a, b);  // And
  or or_1 (or_1_out, and_1_out, and_2_out);
  not not_1 (y, or_1_out);
endmodule
