// Digital circuit Gated-AND-OR-Latch.dig as structural Verilog
module Gated_AND_OR_Latch (
  input  in,
  input  gate,
  output out
);

  wire and_1_out, and_2_out, or_1_out;

  and and_1 (and_1_out, in, gate);
  and and_2 (and_2_out, ~in, gate);  // And
  or or_1 (or_1_out, out, and_1_out);
  and and_3 (out, or_1_out, ~and_2_out);  // And
endmodule
