// Digital circuit RS-NOR-Latch.dig as structural Verilog
module RS_NOR_Latch (
  input  s,
  input  r,
  output out
);

  wire nor_1_out;

  nor nor_1 (nor_1_out, s, out);
  nor nor_2 (out, nor_1_out, r);
endmodule
