// Digital circuit XOR.dig as structural Verilog
module XOR (
  input  a,
  input  b,
  output y
);

  wire and_1_out, and_2_out;

  and and_1 (and_1_out, a, ~b);  // And
  and and_2 (and_2_out, ~a, b);  // And
  or or_1 (y, and_1_out, and_2_out);
endmodule
